# Fritzing sketch lcd_thermostat (saved by Fritzing 0.6.5b)
breadboards: 1

parts:
  Arduino1 = Arduino
  Q1 = NPN-Transistor [package="TO92 [THT]"]
  D1 = Rectifier Diode [part_number=1N4001 package="300 mil [THT]"]
  RE1 = Rotary Encoder [package=THT]
  LCD1 = LCD screen  # not connected
  K1 = Relay [part_number=FRS1B-S package=THT]
  LED1 = LED - 5mm [color="Red (633nm)" package="5 mm [THT]"]  # not connected
  R1 = Resistor [tolerance=±5% resistance=100k package=THT]
  R2 = Resistor [tolerance=±5% resistance=100k package=THT]
  R3 = Resistor [tolerance=±5% resistance=100k package=THT]
  R4 = Resistor [tolerance=±5% resistance=220 package=THT]

nets:
  N1: Arduino1.+5V, D1.cathode, RE1.EncoderPinC, K1.COIL2
  N2: Arduino1.GND, Q1.E, R1.Pin_1, R2.Pin_1, R3.Pin_1
  N3: Q1.B, R4.Pin_1
  N4: Q1.C, D1.anode, K1.COIL1
  N5: RE1.EncoderPinA, R2.Pin_0
  N6: RE1.EncoderPinB, R1.Pin_0
  N7: K1.C1, K1.C2
