# Fritzing sketch lcd_thermostat (saved by Fritzing 0.7.1b)
breadboards: 1

parts:
  Arduino1 = Arduino
  Q1 = NPN-Transistor [package="TO92 [THT]"]
  D1 = Rectifier Diode [part_number=1N4001 package="300 mil [THT]"]
  RE1 = Rotary Encoder [package=THT]
  LCD1 = LCD screen
  K1 = Relay [part_number=FRS1B-S package=THT]
  LED1 = LED - 5mm [color="Red (633nm)" package="5 mm [THT]"]
  R1 = Resistor [tolerance=±5% resistance=100k package=THT]
  R2 = Resistor [tolerance=±5% resistance=100k package=THT]
  R3 = Resistor [tolerance=±5% resistance=100k package=THT]
  R4 = Resistor [tolerance=±5% resistance=220 package=THT]
  R5 = Resistor [tolerance=±5% resistance=220 package=THT]
  R6 = Resistor [tolerance=±5% resistance=220 package=THT]
  R7 = Temperature Sensor (Thermistor) [thermistor_type=NTC package=THT]
  R8 = Resistor [tolerance=±5% resistance=220 package=THT]

nets:
  GND: Arduino1.GND, Q1.E, LCD1.VSS, LCD1.V0, LCD1.LED-, R1.Pin_1, R3.Pin_1, R5.Pin_0, R8.Pin_1
  N1: Arduino1.D13, R6.Pin_1
  N2: Arduino1.D12, LCD1.RS
  N3: Arduino1.D11, LCD1.R/W
  N4: Arduino1.D10, LCD1.E
  N5: Arduino1.D7, RE1.EncoderPinA, R2.Pin_0
  N6: Arduino1.D6, R3.Pin_0
  N7: Arduino1.D5, LCD1.DB4
  N8: Arduino1.D4, LCD1.DB5
  N9: Arduino1.D3, LCD1.DB6
  N10: Arduino1.D2, LCD1.DB7
  +5V: Arduino1.+5V, D1.cathode, RE1.EncoderPinC, LCD1.VDD, K1.COIL2, R7.pin_1
  N11: Arduino1.A0, R7.pin_0, R8.Pin_0
  N12: Arduino1.A1, LED1.cathode
  N13: Arduino1.A2, R4.Pin_0
  N14: Arduino1.A3, RE1.EncoderPinB, R1.Pin_0
  N15: Q1.B, R4.Pin_1
  N16: Q1.C, D1.anode, K1.COIL1
  N17: LCD1.LED+, R6.Pin_0
  N18: K1.C1, K1.C2
  N19: LED1.anode, R5.Pin_1
